# Fritzing sketch Barebone-Arduino-328 (saved by Fritzing 0.8.7b)
breadboards: 1

parts:
  U1 = atmega328 [package=dip]
  JP1 = Header 12 [package=1x12_machine-pin-header_lock.004]
  JP2 = Header 12 [package=1x12_machine-pin-header_lock.004]
  Bauteil1 = FTDI Basic Programmer
  C1 = Capacitor [package=cap-pth-small-kit]
  U2 = Header 1 [package=1x01_offset]
  U3 = Header 1 [package=1x01_offset]
  U4 = Header 1 [package=1x01_offset]
  U5 = Header 1 [package=1x01_offset]
  U6 = Header 1 [package=1x01_offset]
  U7 = Header 1 [package=1x01_offset]
  U8 = Header 1 [package=1x01_offset]
  U9 = Header 1 [package=1x01_offset]
  U10 = Header 1 [package=1x01_offset]
  U11 = Header 1 [package=1x01_offset]
  U12 = Header 1 [package=1x01_offset]
  U13 = Header 1 [package=1x01_offset]
  R1 = Resistor [tolerance=±5% resistance=10k package=THT]

nets:
  N1: U1.RESET, C1.1, U5.1, R1.Pin_0
  N2: U1.D0_(RX), Bauteil1.TXO, U4.1
  N3: U1.D1_(TX), JP1.12, Bauteil1.RXI
  N4: U1.D2, JP1.11
  N5: U1.D3_(PWM), JP1.10
  N6: U1.D4, JP1.9
  N7: U1.VCC, U1.AVCC, JP1.8, JP2.6, Bauteil1.POWER, U6.1, U7.1, U8.1, U9.1, R1.Pin_1
  GND: U1.GND, JP1.7, JP2.8, Bauteil1.GND, U10.1, U11.1, U12.1, U13.1
  N8: U1.XLAT1, JP1.6
  N9: U1.XLAT2, JP1.5
  N10: U1.D5_(PWM), JP1.4
  N11: U1.D6_(PWM), JP1.3
  N12: U1.D7, JP1.2
  N13: U1.D8, JP1.1
  N14: U1.D9_(PWM), JP2.1
  N15: U1.D10_(PWM), JP2.2
  N16: U1.D11_(PWM), JP2.3
  N17: U1.D12, JP2.4
  N18: U1.D13, JP2.5
  N19: U1.AREF, JP2.7
  N20: U1.A0, JP2.9
  N21: U1.A1, JP2.10
  N22: U1.A2, JP2.11
  N23: U1.A3, JP2.12
  N24: U1.A4, U2.1
  N25: U1.A5, U3.1
  N26: Bauteil1.DTR, C1.2
